# Fritzing sketch esquema (saved by Fritzing 0.9.3b)
breadboards: 1

parts:
  U1 = ST7735 1.8 inch TFT LCD [package="SIP (Single Inline) [THT]"]
  Part1 = Arduino Uno (Rev3)
  S1 = Pushbutton [package="[THT]"]
  S2 = Pushbutton [package="[THT]"]
  S3 = Pushbutton [package="[THT]"]
  R1 = Resistor [tolerance=±5% resistance=220 package=THT]
  R2 = Resistor [tolerance=±5% resistance=220 package=THT]
  R3 = Resistor [tolerance=±5% resistance=220 package=THT]

nets:
  N1: U1.VLED, Part1.3V3
  N2: U1.RST, Part1.D8
  N3: U1.A0, Part1.D9_PWM
  N4: U1.SDA, Part1.D11_PWM/MOSI
  N5: U1.SCK, Part1.D13/SCK
  VCC: U1.VCC, Part1.5V, S1.Pin_3, S1.Pin_4, S2.Pin_3, S2.Pin_4, S3.Pin_3, S3.Pin_4
  N6: U1.CS, Part1.D10_PWM/SS
  GND: U1.GND, Part1.GND, R1.Pin_1, R2.Pin_1, R3.Pin_1
  N7: Part1.D2, S3.Pin_1, S3.Pin_2, R3.Pin_0
  N8: Part1.D3_PWM, S2.Pin_1, S2.Pin_2, R2.Pin_0
  N9: Part1.D4, S1.Pin_1, S1.Pin_2, R1.Pin_0

custom parts:
  ST7735 1.8 inch TFT LCD: 1.8 inch TFT LCD module. SPI interface, ST7735 controller
